// Digital circuit ALU_Integração.dig as structural Verilog
module \ALU_Integração  (
  input  [2:0] OP,
  input  [7:0] A,
  input  [7:0] B,
  input  CLOCK,
  input  STORE,
  input  START,
  input  SUB,
  output [7:0] S,
  output [7:0] S_AC,
  output [15:0] R_MULT
);

  wire R_ADD, R_NAND, R_SHL, R_SHR, R_XOR, somador_subtrator_8bits_1_p4;

  // somador_subtrator_8bits somador_subtrator_8bits_1: pin names not known; wires that end beside it: A, B, SUB, somador_subtrator_8bits_1_p4, R_ADD
  // XOR xor_1: pin names not known; wires that end beside it: A, B, R_XOR
  // NAND nand_1: pin names not known; wires that end beside it: A, B, R_NAND
  // Shift_Left shift_left_1: pin names not known; wires that end beside it: A, R_SHL
  // Shift_Right shift_right_1: pin names not known; wires that end beside it: A, R_SHR
  // multiplicador_8bits multiplicador_8bits_1: pin names not known; wires that end beside it: A, STORE, CLOCK, B, START, R_MULT[15:8], R_MULT[7:0]
  LED OVERFLOW (.in(somador_subtrator_8bits_1_p4));
  // Seletor seletor_1: pin names not known; wires that end beside it: R_ADD, R_ADD, R_XOR, R_NAND, R_SHL, R_SHR, R_MULT[7:0], {8{1'b0}}, OP, S
  // REG_AC_8Bit reg_ac_8bit_1: pin names not known; wires that end beside it: S, STORE, CLOCK, S_AC

  // Other names for the same wires on the sheet: DATA[7:0] = S; MSB[7:0] = R_MULT[15:8]; LSB[7:0] = R_MULT[7:0];
  //   R_MULT_t[7:0] = R_MULT[7:0]

  // Notes on the sheet:
  //   OP0 - Adição
  //   OP1 - Subtração
  //   OP6 - Multiplicação
  //   ALU - Integração
  //   Aqui estaremos integrando todos os módulos criados
endmodule
